# Fritzing sketch DosingCircuit (saved by Fritzing 0.9.10b)
breadboards: 1

parts:
  DC_INput = female pin header, 4 pins [form="♀ (female)"]
  Motor1 = female pin header, 2 pins [form="♀ (female)"]
  Motor2 = female pin header, 2 pins [form="♀ (female)"]
  Motor3 = female pin header, 2 pins [form="♀ (female)"]
  Motor4 = female pin header, 2 pins [form="♀ (female)"]
  jumper = female pin header, 2 pins [form="♀ (female)"]
  Voltage_Selector = male pin header, 3 pins [form="♂ (male)"]
  IC1 = ULN2803A [package=THT]
  GPIO_input = female pin header, 4 pins [form="♀ (female)"]
  limit_resistors = Resistor [tolerance=±5% power=0.25 resistance=1.3k package=THT]
  R11 = Resistor [tolerance=±5% power=0.25 resistance=1.3k package=THT]
  R12 = Resistor [tolerance=±5% power=0.25 resistance=1.3k package=THT]
  R13 = Resistor [tolerance=±5% power=0.25 resistance=1.3k package=THT]

nets:
  N1: DC_INput.pin1, Voltage_Selector.pin1
  GND: DC_INput.pin2, DC_INput.pin3, IC1.0V
  N2: DC_INput.pin4, Voltage_Selector.pin2
  N3: Motor1.pin1, Motor2.pin1, Motor3.pin1, Motor4.pin1, Voltage_Selector.pin3, IC1.COM_-_Common
  N4: Motor1.pin2, IC1.Out_1
  N5: Motor2.pin2, IC1.Out_3
  N6: Motor3.pin2, IC1.Out_5
  N7: Motor4.pin2, IC1.Out_7
  N8: jumper.pin1, jumper.pin2
  N9: IC1.In_1, limit_resistors.Pin_1
  N10: IC1.In_3, R11.Pin_1
  N11: IC1.In_5, R12.Pin_1
  N12: IC1.In_7, R13.Pin_1
  N13: GPIO_input.pin1, limit_resistors.Pin_0
  N14: GPIO_input.pin2, R11.Pin_0
  N15: GPIO_input.pin3, R12.Pin_0
  N16: GPIO_input.pin4, R13.Pin_0

notes:
  12VDC
  5VDC
  GND
